# Fritzing sketch sender (saved by Fritzing 0.9.5d)
breadboards: 1

parts:
  Ebyte_transceiver = ossoyoo-lora-module
  VCC2 = Battery
  Arduino_Nano = Arduino Nano (Rev3.0)
  S1 = Pushbutton [package="[THT]"]
  R1 = Resistor [tolerance=±5% resistance=220 package=THT]
  OLED_I2C1 = OLED 128x64 I2C Monochrome Display

nets:
  N1: Ebyte_transceiver.M0, Arduino_Nano.D6
  N2: Ebyte_transceiver.M1, Arduino_Nano.D5
  N3: Ebyte_transceiver.RXD, Arduino_Nano.D3
  N4: Ebyte_transceiver.TXD, Arduino_Nano.D4
  N5: Ebyte_transceiver.AUX, Arduino_Nano.D2
  GND: VCC2.-, Arduino_Nano.GND, R1.Pin_0, OLED_I2C1.GND
  N6: VCC2.+, Arduino_Nano.VIN
  N7: Arduino_Nano.D7, S1.Pin_1, S1.Pin_2, R1.Pin_1
  5V: Arduino_Nano.5V, S1.Pin_3, S1.Pin_4, OLED_I2C1.VDD
  N8: Arduino_Nano.A5, OLED_I2C1.SCK
  N9: Arduino_Nano.A4, OLED_I2C1.SDA

notes:
  Sender / Émetteur

custom parts:
  ossoyoo-lora-module: Osoyoo Long Distance wireless transceiver Uart LoRa Module.
  Battery: Your standard 2x 18650 battery pack (7,4 Volts)

// code stored in the sketch: sonnette_receiver.ino
#include <SoftwareSerial.h>
#include "EBYTE.h"

#define PIN_AX 2
#define PIN_TX 4
#define PIN_RX 3
#define PIN_M1 5
#define PIN_M0 6
#define BTN    7

struct DATA {
  int State;
};

DATA Message;

SoftwareSerial ESerial(PIN_RX, PIN_TX);
EBYTE Transceiver(&ESerial, PIN_M0, PIN_M1, PIN_AX);

void setup() {
  ESerial.begin(9600);
  pinMode(LED_BUILTIN, OUTPUT);
  pinMode(BTN, INPUT_PULLUP);
  Transceiver.init();
  Transceiver.PrintParameters();
}

void loop() {
  if (digitalRead(BTN) == HIGH){
    Message.State = 1;
    Transceiver.SendStruct(&Message, sizeof(Message));
    for (int i = 0; i <= 125; i++) {
      digitalWrite(LED_BUILTIN, HIGH);
      delay(50);
      digitalWrite(LED_BUILTIN, LOW);
      delay(50);
    }
  } else {
    digitalWrite(LED_BUILTIN, LOW);
  }
}
